// Logisim project Timofeev_Maksunova_Peshkov_24214_main.circ as structural Verilog: 5 circuits, main circuit random
module main (
);

  wire and_1_out, and_2_out, and_3_out, bitselector_9_out, button_5_out, button_6_out, cdm_16_1_p3,
       cdm_16_1_p10, cdm_16_1_p12, cdm_16_1_p14, choosing_move, clock_2_out, clock_3_out, clock_4_out,
       comparator_1_eq, comparator_2_lt, comparator_3_lt, comparator_4_gt, comparator_5_eq, comparator_6_eq,
       comparator_7_eq, comparator_8_eq, comparator_9_eq, comparator_10_eq, comparator_11_eq, D,
       demultiplexer_2_out0, demultiplexer_2_out1, demultiplexer_2_out2, demultiplexer_2_out3, evaluating,
       is_ai, L, mem, not_1_out, not_2_out, not_3_out, R, read, ready, simulating, small_comparator_1_out_3,
       small_comparator_2_out_3, small_comparator_3_out_3, small_comparator_4_out_3,
       small_comparator_5_out_3, small_comparator_6_out_3, small_comparator_7_out_3,
       small_comparator_8_out_3, small_comparator_9_out_3, small_comparator_10_out_3,
       small_comparator_11_out_3, small_comparator_12_out_3, small_comparator_13_out_3,
       small_comparator_14_out_3, small_comparator_15_out_3, small_comparator_16_out_3, U, word;
  wire [1:0] bitselector_7_out;
  wire [3:0] _0_i, _0_o, _1_i, _1_o, _2_i, _2_o, _3_i, _3_o, _4_i, _4_o, _5_i, _5_o, _6_i, _6_o, _7_i, _7_o,
       _8_i, _8_o, _9_i, _9_o, _10_i, _10_o, _11_i, _11_o, _12_i, _12_o, _13_i, _13_o, _14_i, _14_o, _15_i,
       _15_o, bitselector_5_out, bitselector_8_out;
  wire [7:0] bitselector_1_out, bitselector_2_out, bitselector_3_out, bitselector_4_out, bitselector_6_out;
  wire [15:0] address_bus, cdm_16_1_p20, cdm_16_1_p21, data, data_bus, game_over_check_1_end,
       input_controller_1_out_5, multiplexer_1_out, multiplexer_2_out, multiplexer_3_out, r0, r1, r2, r3, r4,
       r5, r6, r7, random_1_out_2;
  wire [18:0] main_1_out_2, main_1_out_3, main_1_out_4, main_1_out_5, main_1_out_6, main_1_out_7,
       main_1_out_8, main_1_out_9, main_1_out_10, main_1_out_11, main_1_out_12, main_1_out_13, main_1_out_14,
       main_1_out_15, main_1_out_16, main_1_out_17, main_1_out_18, main_1_out_19, main_1_out_20,
       main_2_out_2, main_2_out_3, main_2_out_4, main_2_out_5, main_2_out_6, main_2_out_7, main_2_out_8,
       main_2_out_9, main_2_out_10, main_2_out_11, main_2_out_12, main_2_out_13, main_2_out_14,
       main_2_out_15, main_2_out_16, main_2_out_17, main_2_out_18, main_2_out_19, main_2_out_20,
       main_3_out_2, main_3_out_3, main_3_out_4, main_3_out_5, main_3_out_6, main_3_out_7, main_3_out_8,
       main_3_out_9, main_3_out_10, main_3_out_11, main_3_out_12, main_3_out_13, main_3_out_14,
       main_3_out_15, main_3_out_16, main_3_out_17, main_3_out_18, main_3_out_19, main_3_out_20,
       main_4_out_2, main_4_out_3, main_4_out_4, main_4_out_5, main_4_out_6, main_4_out_7, main_4_out_8,
       main_4_out_9, main_4_out_10, main_4_out_11, main_4_out_12, main_4_out_13, main_4_out_14,
       main_4_out_15, main_4_out_16, main_4_out_17, main_4_out_18, main_4_out_19, main_4_out_20,
       main_5_out_2, main_5_out_3, main_5_out_4, main_5_out_5, main_5_out_6, main_5_out_7, main_5_out_8,
       main_5_out_9, main_5_out_10, main_5_out_11, main_5_out_12, main_5_out_13, main_5_out_14,
       main_5_out_15, main_5_out_16, main_5_out_17, main_5_out_18, main_5_out_19, main_5_out_20,
       main_6_out_2, main_6_out_3, main_6_out_4, main_6_out_5, main_6_out_6, main_6_out_7, main_6_out_8,
       main_6_out_9, main_6_out_10, main_6_out_11, main_6_out_12, main_6_out_13, main_6_out_14,
       main_6_out_15, main_6_out_16, main_6_out_17, main_6_out_18, main_6_out_19, main_6_out_20,
       main_7_out_2, main_7_out_3, main_7_out_4, main_7_out_5, main_7_out_6, main_7_out_7, main_7_out_8,
       main_7_out_9, main_7_out_10, main_7_out_11, main_7_out_12, main_7_out_13, main_7_out_14,
       main_7_out_15, main_7_out_16, main_7_out_17, main_7_out_18, main_7_out_19, main_7_out_20,
       main_8_out_2, main_8_out_3, main_8_out_4, main_8_out_5, main_8_out_6, main_8_out_7, main_8_out_8,
       main_8_out_9, main_8_out_10, main_8_out_11, main_8_out_12, main_8_out_13, main_8_out_14,
       main_8_out_15, main_8_out_16, main_8_out_17, main_8_out_18, main_8_out_19, main_8_out_20,
       main_9_out_2, main_9_out_3, main_9_out_4, main_9_out_5, main_9_out_6, main_9_out_7, main_9_out_8,
       main_9_out_9, main_9_out_10, main_9_out_11, main_9_out_12, main_9_out_13, main_9_out_14,
       main_9_out_15, main_9_out_16, main_9_out_17, main_9_out_18, main_9_out_19, main_9_out_20,
       main_10_out_2, main_10_out_3, main_10_out_4, main_10_out_5, main_10_out_6, main_10_out_7,
       main_10_out_8, main_10_out_9, main_10_out_10, main_10_out_11, main_10_out_12, main_10_out_13,
       main_10_out_14, main_10_out_15, main_10_out_16, main_10_out_17, main_10_out_18, main_10_out_19,
       main_10_out_20, main_11_out_2, main_11_out_3, main_11_out_4, main_11_out_5, main_11_out_6,
       main_11_out_7, main_11_out_8, main_11_out_9, main_11_out_10, main_11_out_11, main_11_out_12,
       main_11_out_13, main_11_out_14, main_11_out_15, main_11_out_16, main_11_out_17, main_11_out_18,
       main_11_out_19, main_11_out_20, main_12_out_2, main_12_out_3, main_12_out_4, main_12_out_5,
       main_12_out_6, main_12_out_7, main_12_out_8, main_12_out_9, main_12_out_10, main_12_out_11,
       main_12_out_12, main_12_out_13, main_12_out_14, main_12_out_15, main_12_out_16, main_12_out_17,
       main_12_out_18, main_12_out_19, main_12_out_20, main_13_out_2, main_13_out_3, main_13_out_4,
       main_13_out_5, main_13_out_6, main_13_out_7, main_13_out_8, main_13_out_9, main_13_out_10,
       main_13_out_11, main_13_out_12, main_13_out_13, main_13_out_14, main_13_out_15, main_13_out_16,
       main_13_out_17, main_13_out_18, main_13_out_19, main_13_out_20, main_14_out_2, main_14_out_3,
       main_14_out_4, main_14_out_5, main_14_out_6, main_14_out_7, main_14_out_8, main_14_out_9,
       main_14_out_10, main_14_out_11, main_14_out_12, main_14_out_13, main_14_out_14, main_14_out_15,
       main_14_out_16, main_14_out_17, main_14_out_18, main_14_out_19, main_14_out_20, main_15_out_2,
       main_15_out_3, main_15_out_4, main_15_out_5, main_15_out_6, main_15_out_7, main_15_out_8,
       main_15_out_9, main_15_out_10, main_15_out_11, main_15_out_12, main_15_out_13, main_15_out_14,
       main_15_out_15, main_15_out_16, main_15_out_17, main_15_out_18, main_15_out_19, main_15_out_20,
       main_16_out_2, main_16_out_3, main_16_out_4, main_16_out_5, main_16_out_6, main_16_out_7,
       main_16_out_8, main_16_out_9, main_16_out_10, main_16_out_11, main_16_out_12, main_16_out_13,
       main_16_out_14, main_16_out_15, main_16_out_16, main_16_out_17, main_16_out_18, main_16_out_19,
       main_16_out_20;

  // CdM_16 cdm_16_1: pin names not known; wires that end beside it: r0, r1, cdm_16_1_p3, r2, r3, r4, r5, r6, r7, cdm_16_1_p10, cdm_16_1_p10, cdm_16_1_p12, cdm_16_1_p12, cdm_16_1_p14, cdm_16_1_p14, mem, read, word, address_bus, cdm_16_1_p20, cdm_16_1_p21
  Clock clock_1 (.out(cdm_16_1_p3));
  Clock clock_2 (.out(clock_2_out));
  BitSelector #(.width(16), .group(8)) bitselector_1 (.in(address_bus), .out(bitselector_1_out), .sel(1'b1));
  not not_1 (not_1_out, read);
  BitSelector #(.width(16), .group(8)) bitselector_2 (.in(address_bus), .out(bitselector_2_out), .sel(1'b0));
  BitSelector #(.width(16), .group(8)) bitselector_3 (.in(address_bus), .out(bitselector_3_out), .sel(1'b0));
  BitSelector #(.width(16), .group(8)) bitselector_4 (.in(address_bus), .out(bitselector_4_out), .sel(1'b0));
  random random_1 (.in_1(comparator_1_eq), .out_2(random_1_out_2));
  Comparator #(.width(16), .mode("unsigned")) comparator_1 (
    .a(16'hfefe), .b(address_bus), .eq(comparator_1_eq));  // open: gt, lt
  and and_1 (and_1_out, bitselector_1_out[0], bitselector_1_out[1], bitselector_1_out[2], bitselector_1_out[3], bitselector_1_out[4], bitselector_1_out[5], bitselector_1_out[6], bitselector_1_out[7], mem, not_1_out, comparator_2_lt);
  Comparator #(.mode("unsigned")) comparator_2 (
    .a(bitselector_2_out), .b(8'h10), .lt(comparator_2_lt));  // open: gt, eq
  BitSelector #(.width(16), .group(4)) bitselector_5 (.in(address_bus), .out(bitselector_5_out), .sel(2'b00));
  BitSelector #(.width(16), .group(8)) bitselector_6 (.in(address_bus), .out(bitselector_6_out), .sel(1'b1));
  not not_2 (not_2_out, read);
  Comparator #(.mode("unsigned")) comparator_3 (
    .a(bitselector_3_out), .b(8'h65), .lt(comparator_3_lt));  // open: gt, eq
  and and_2 (and_2_out, comparator_3_lt, comparator_4_gt);
  Comparator #(.mode("unsigned")) comparator_4 (
    .a(bitselector_4_out), .b(8'h5f), .gt(comparator_4_gt));  // open: eq, lt
  Multiplexer #(.width(16), .enable("false")) multiplexer_1 (
    .in0(data_bus), .in1(random_1_out_2), .out(multiplexer_1_out), .sel(comparator_1_eq));
  assign data_bus = not_3_out ? cdm_16_1_p20 : 16'bz;  // Controlled_Buffer controlled_buffer_1
  not not_3 (not_3_out, read);
  Controlled_Buffer #(.width(16)) controlled_buffer_2 (.in(data_bus), .en(read));  // open: out
  assign cdm_16_1_p21 = read ? data : 16'bz;  // Controlled_Buffer controlled_buffer_3
  small_comparator small_comparator_1 (.in_1(4'b0000), .in_2(bitselector_5_out), .out_3(small_comparator_1_out_3));
  small_comparator small_comparator_2 (.in_1(4'b0001), .in_2(bitselector_5_out), .out_3(small_comparator_2_out_3));
  small_comparator small_comparator_3 (.in_1(4'b0010), .in_2(bitselector_5_out), .out_3(small_comparator_3_out_3));
  small_comparator small_comparator_4 (.in_1(4'b0011), .in_2(bitselector_5_out), .out_3(small_comparator_4_out_3));
  small_comparator small_comparator_5 (.in_1(4'b0100), .in_2(bitselector_5_out), .out_3(small_comparator_5_out_3));
  small_comparator small_comparator_6 (.in_1(4'b0101), .in_2(bitselector_5_out), .out_3(small_comparator_6_out_3));
  small_comparator small_comparator_7 (.in_1(4'b0110), .in_2(bitselector_5_out), .out_3(small_comparator_7_out_3));
  small_comparator small_comparator_8 (.in_1(4'b0111), .in_2(bitselector_5_out), .out_3(small_comparator_8_out_3));
  small_comparator small_comparator_9 (.in_1(4'b1000), .in_2(bitselector_5_out), .out_3(small_comparator_9_out_3));
  small_comparator small_comparator_10 (.in_1(4'b1001), .in_2(bitselector_5_out), .out_3(small_comparator_10_out_3));
  small_comparator small_comparator_11 (.in_1(4'b1010), .in_2(bitselector_5_out), .out_3(small_comparator_11_out_3));
  small_comparator small_comparator_12 (.in_1(4'b1011), .in_2(bitselector_5_out), .out_3(small_comparator_12_out_3));
  small_comparator small_comparator_13 (.in_1(4'b1100), .in_2(bitselector_5_out), .out_3(small_comparator_13_out_3));
  small_comparator small_comparator_14 (.in_1(4'b1101), .in_2(bitselector_5_out), .out_3(small_comparator_14_out_3));
  small_comparator small_comparator_15 (.in_1(4'b1110), .in_2(bitselector_5_out), .out_3(small_comparator_15_out_3));
  small_comparator small_comparator_16 (.in_1(4'b1111), .in_2(bitselector_5_out), .out_3(small_comparator_16_out_3));
  and and_3 (and_3_out, bitselector_6_out[0], bitselector_6_out[1], bitselector_6_out[2], bitselector_6_out[3], bitselector_6_out[4], bitselector_6_out[5], bitselector_6_out[6], bitselector_6_out[7], mem, not_2_out, and_2_out);
  BitSelector #(.width(16), .group(2)) bitselector_7 (.in(address_bus), .out(bitselector_7_out), .sel(3'b000));
  BitSelector #(.width(16), .group(4)) bitselector_8 (.in(data_bus), .out(bitselector_8_out), .sel(2'b00));
  Demultiplexer #(.select(4), .width(4)) demultiplexer_1 (
    .out0(_0_i), .out1(_1_i), .out2(_2_i), .out3(_3_i), .out4(_4_i), .out5(_5_i), .out6(_6_i), .out7(_7_i),
    .out8(_8_i), .out9(_9_i), .out10(_10_i), .out11(_11_i), .out12(_12_i), .out13(_13_i), .out14(_14_i),
    .out15(_15_i), .in(bitselector_8_out), .sel(bitselector_5_out), .en(and_1_out));
  Clock clock_3 (.out(clock_3_out));
  BitSelector #(.width(16)) bitselector_9 (.in(data_bus), .out(bitselector_9_out), .sel(4'b0000));
  Demultiplexer #(.select(2)) demultiplexer_2 (
    .out0(demultiplexer_2_out0), .out1(demultiplexer_2_out1), .out2(demultiplexer_2_out2),
    .out3(demultiplexer_2_out3), .in(bitselector_9_out), .sel(bitselector_7_out), .en(and_3_out));
  game_over_check game_over_check_1 (
    ._0(_0_o), ._1(_1_o), ._2(_2_o), ._3(_3_o), ._4(_4_o), ._5(_5_o), ._6(_6_o), ._7(_7_o), ._8(_8_o),
    ._9(_9_o), ._10(_10_o), ._11(_11_o), ._12(_12_o), ._13(_13_o), ._14(_14_o), ._15(_15_o),
    .\end (game_over_check_1_end));
  Clock clock_4 (.out(clock_4_out));
  Register #(.width(4)) register_1 (.D(_0_i), .en(small_comparator_1_out_3), .Q(_0_o), .clk(clock_2_out));  // open: clr
  Register #(.width(4)) register_2 (.D(_4_i), .en(small_comparator_5_out_3), .Q(_4_o), .clk(clock_2_out));  // open: clr
  Register #(.width(4)) register_3 (.D(_8_i), .en(small_comparator_9_out_3), .Q(_8_o), .clk(clock_2_out));  // open: clr
  Register #(.width(4)) register_4 (
    .D(_12_i), .en(small_comparator_13_out_3), .Q(_12_o), .clk(clock_2_out));  // open: clr
  Comparator #(.width(2)) comparator_5 (.a(2'b00), .b(bitselector_7_out), .eq(comparator_5_eq));  // open: gt, lt
  Comparator #(.width(2)) comparator_6 (.a(2'b01), .b(bitselector_7_out), .eq(comparator_6_eq));  // open: gt, lt
  Comparator #(.width(2)) comparator_7 (.a(2'b10), .b(bitselector_7_out), .eq(comparator_7_eq));  // open: gt, lt
  Comparator #(.width(2)) comparator_8 (.a(2'b11), .b(bitselector_7_out), .eq(comparator_8_eq));  // open: gt, lt
  Comparator #(.width(16), .mode("unsigned")) comparator_9 (
    .a(16'hfefc), .b(address_bus), .eq(comparator_9_eq));  // open: gt, lt
  // RAM ram_1: pin names not known; wires that end beside it: address_bus, word, mem, clock_4_out, read, data_bus
  Register #(.width(4)) register_5 (.D(_1_i), .en(small_comparator_2_out_3), .Q(_1_o), .clk(clock_2_out));  // open: clr
  Register #(.width(4)) register_6 (.D(_5_i), .en(small_comparator_6_out_3), .Q(_5_o), .clk(clock_2_out));  // open: clr
  Register #(.width(4)) register_7 (
    .D(_9_i), .en(small_comparator_10_out_3), .Q(_9_o), .clk(clock_2_out));  // open: clr
  Register #(.width(4)) register_8 (
    .D(_13_i), .en(small_comparator_14_out_3), .Q(_13_o), .clk(clock_2_out));  // open: clr
  Register #(.width(1)) register_9 (
    .D(demultiplexer_2_out0), .en(comparator_5_eq), .Q(ready), .clk(clock_3_out));  // open: clr
  Register #(.width(1)) register_10 (
    .D(demultiplexer_2_out2), .en(comparator_7_eq), .Q(evaluating), .clk(clock_3_out));  // open: clr
  Register #(.width(1)) register_11 (
    .D(demultiplexer_2_out1), .en(comparator_6_eq), .Q(simulating), .clk(clock_3_out));  // open: clr
  Multiplexer #(.width(16), .enable("false")) multiplexer_2 (
    .in0(multiplexer_1_out), .in1(game_over_check_1_end), .out(multiplexer_2_out), .sel(comparator_9_eq));
  Register #(.width(4)) register_12 (
    .D(_2_i), .en(small_comparator_3_out_3), .Q(_2_o), .clk(clock_2_out));  // open: clr
  Register #(.width(4)) register_13 (
    .D(_6_i), .en(small_comparator_7_out_3), .Q(_6_o), .clk(clock_2_out));  // open: clr
  Register #(.width(4)) register_14 (
    .D(_10_i), .en(small_comparator_11_out_3), .Q(_10_o), .clk(clock_2_out));  // open: clr
  Register #(.width(4)) register_15 (
    .D(_14_i), .en(small_comparator_15_out_3), .Q(_14_o), .clk(clock_2_out));  // open: clr
  Register #(.width(1)) register_16 (
    .D(demultiplexer_2_out3), .en(comparator_8_eq), .Q(choosing_move), .clk(clock_3_out));  // open: clr
  Register #(.width(4)) register_17 (
    .D(_3_i), .en(small_comparator_4_out_3), .Q(_3_o), .clk(clock_2_out));  // open: clr
  Register #(.width(4)) register_18 (
    .D(_7_i), .en(small_comparator_8_out_3), .Q(_7_o), .clk(clock_2_out));  // open: clr
  Register #(.width(4)) register_19 (
    .D(_11_i), .en(small_comparator_12_out_3), .Q(_11_o), .clk(clock_2_out));  // open: clr
  Register #(.width(4)) register_20 (
    .D(_15_i), .en(small_comparator_16_out_3), .Q(_15_o), .clk(clock_2_out));  // open: clr
  input_controller input_controller_1 (.LEFT(L), .in_2(R), .DOWN(D), .in_4(U), .out_5(input_controller_1_out_5));
  Comparator #(.width(16), .mode("unsigned")) comparator_10 (
    .a(16'hfefa), .b(address_bus), .eq(comparator_10_eq));  // open: gt, lt
  Timofeev_Maksunova_Peshkov_24214_number_picker_main main_1 (
    .in_1(_0_o), .out_2(main_1_out_2), .out_3(main_1_out_3), .out_4(main_1_out_4), .out_5(main_1_out_5),
    .out_6(main_1_out_6), .out_7(main_1_out_7), .out_8(main_1_out_8), .out_9(main_1_out_9),
    .out_10(main_1_out_10), .out_11(main_1_out_11), .out_12(main_1_out_12), .out_13(main_1_out_13),
    .out_14(main_1_out_14), .out_15(main_1_out_15), .out_16(main_1_out_16), .out_17(main_1_out_17),
    .out_18(main_1_out_18), .out_19(main_1_out_19), .out_20(main_1_out_20));
  DotMatrix #(.matrixcols(19), .matrixrows(19)) dotmatrix_1 (
    .col0(main_1_out_2), .col1(main_1_out_6), .col2(main_1_out_10), .col3(main_1_out_14),
    .col4(main_1_out_18), .col5(main_1_out_3), .col6(main_1_out_7), .col7(main_1_out_11),
    .col8(main_1_out_15), .col9(main_1_out_19), .col10(main_1_out_4), .col11(main_1_out_8),
    .col12(main_1_out_12), .col13(main_1_out_16), .col14(main_1_out_20), .col15(main_1_out_5),
    .col16(main_1_out_9), .col17(main_1_out_13), .col18(main_1_out_17));
  Timofeev_Maksunova_Peshkov_24214_number_picker_main main_2 (
    .in_1(_4_o), .out_2(main_2_out_2), .out_3(main_2_out_3), .out_4(main_2_out_4), .out_5(main_2_out_5),
    .out_6(main_2_out_6), .out_7(main_2_out_7), .out_8(main_2_out_8), .out_9(main_2_out_9),
    .out_10(main_2_out_10), .out_11(main_2_out_11), .out_12(main_2_out_12), .out_13(main_2_out_13),
    .out_14(main_2_out_14), .out_15(main_2_out_15), .out_16(main_2_out_16), .out_17(main_2_out_17),
    .out_18(main_2_out_18), .out_19(main_2_out_19), .out_20(main_2_out_20));
  DotMatrix #(.matrixcols(19), .matrixrows(19)) dotmatrix_2 (
    .col0(main_2_out_2), .col1(main_2_out_6), .col2(main_2_out_10), .col3(main_2_out_14),
    .col4(main_2_out_18), .col5(main_2_out_3), .col6(main_2_out_7), .col7(main_2_out_11),
    .col8(main_2_out_15), .col9(main_2_out_19), .col10(main_2_out_4), .col11(main_2_out_8),
    .col12(main_2_out_12), .col13(main_2_out_16), .col14(main_2_out_20), .col15(main_2_out_5),
    .col16(main_2_out_9), .col17(main_2_out_13), .col18(main_2_out_17));
  Timofeev_Maksunova_Peshkov_24214_number_picker_main main_3 (
    .in_1(_8_o), .out_2(main_3_out_2), .out_3(main_3_out_3), .out_4(main_3_out_4), .out_5(main_3_out_5),
    .out_6(main_3_out_6), .out_7(main_3_out_7), .out_8(main_3_out_8), .out_9(main_3_out_9),
    .out_10(main_3_out_10), .out_11(main_3_out_11), .out_12(main_3_out_12), .out_13(main_3_out_13),
    .out_14(main_3_out_14), .out_15(main_3_out_15), .out_16(main_3_out_16), .out_17(main_3_out_17),
    .out_18(main_3_out_18), .out_19(main_3_out_19), .out_20(main_3_out_20));
  DotMatrix #(.matrixcols(19), .matrixrows(19)) dotmatrix_3 (
    .col0(main_3_out_2), .col1(main_3_out_6), .col2(main_3_out_10), .col3(main_3_out_14),
    .col4(main_3_out_18), .col5(main_3_out_3), .col6(main_3_out_7), .col7(main_3_out_11),
    .col8(main_3_out_15), .col9(main_3_out_19), .col10(main_3_out_4), .col11(main_3_out_8),
    .col12(main_3_out_12), .col13(main_3_out_16), .col14(main_3_out_20), .col15(main_3_out_5),
    .col16(main_3_out_9), .col17(main_3_out_13), .col18(main_3_out_17));
  DotMatrix #(.matrixcols(19), .matrixrows(19)) dotmatrix_4 (
    .col0(main_4_out_2), .col1(main_4_out_6), .col2(main_4_out_10), .col3(main_4_out_14),
    .col4(main_4_out_18), .col5(main_4_out_3), .col6(main_4_out_7), .col7(main_4_out_11),
    .col8(main_4_out_15), .col9(main_4_out_19), .col10(main_4_out_4), .col11(main_4_out_8),
    .col12(main_4_out_12), .col13(main_4_out_16), .col14(main_4_out_20), .col15(main_4_out_5),
    .col16(main_4_out_9), .col17(main_4_out_13), .col18(main_4_out_17));
  Timofeev_Maksunova_Peshkov_24214_number_picker_main main_4 (
    .in_1(_12_o), .out_2(main_4_out_2), .out_3(main_4_out_3), .out_4(main_4_out_4), .out_5(main_4_out_5),
    .out_6(main_4_out_6), .out_7(main_4_out_7), .out_8(main_4_out_8), .out_9(main_4_out_9),
    .out_10(main_4_out_10), .out_11(main_4_out_11), .out_12(main_4_out_12), .out_13(main_4_out_13),
    .out_14(main_4_out_14), .out_15(main_4_out_15), .out_16(main_4_out_16), .out_17(main_4_out_17),
    .out_18(main_4_out_18), .out_19(main_4_out_19), .out_20(main_4_out_20));
  Multiplexer #(.width(16), .enable("false")) multiplexer_3 (
    .in0(multiplexer_2_out), .in1(input_controller_1_out_5), .out(multiplexer_3_out), .sel(comparator_10_eq));
  LED led_1 (.in(simulating));
  LED led_2 (.in(evaluating));
  LED led_3 (.in(choosing_move));
  DotMatrix #(.matrixcols(19), .matrixrows(19)) dotmatrix_5 (
    .col0(main_5_out_2), .col1(main_5_out_6), .col2(main_5_out_10), .col3(main_5_out_14),
    .col4(main_5_out_18), .col5(main_5_out_3), .col6(main_5_out_7), .col7(main_5_out_11),
    .col8(main_5_out_15), .col9(main_5_out_19), .col10(main_5_out_4), .col11(main_5_out_8),
    .col12(main_5_out_12), .col13(main_5_out_16), .col14(main_5_out_20), .col15(main_5_out_5),
    .col16(main_5_out_9), .col17(main_5_out_13), .col18(main_5_out_17));
  Timofeev_Maksunova_Peshkov_24214_number_picker_main main_5 (
    .in_1(_1_o), .out_2(main_5_out_2), .out_3(main_5_out_3), .out_4(main_5_out_4), .out_5(main_5_out_5),
    .out_6(main_5_out_6), .out_7(main_5_out_7), .out_8(main_5_out_8), .out_9(main_5_out_9),
    .out_10(main_5_out_10), .out_11(main_5_out_11), .out_12(main_5_out_12), .out_13(main_5_out_13),
    .out_14(main_5_out_14), .out_15(main_5_out_15), .out_16(main_5_out_16), .out_17(main_5_out_17),
    .out_18(main_5_out_18), .out_19(main_5_out_19), .out_20(main_5_out_20));
  DotMatrix #(.matrixcols(19), .matrixrows(19)) dotmatrix_6 (
    .col0(main_6_out_2), .col1(main_6_out_6), .col2(main_6_out_10), .col3(main_6_out_14),
    .col4(main_6_out_18), .col5(main_6_out_3), .col6(main_6_out_7), .col7(main_6_out_11),
    .col8(main_6_out_15), .col9(main_6_out_19), .col10(main_6_out_4), .col11(main_6_out_8),
    .col12(main_6_out_12), .col13(main_6_out_16), .col14(main_6_out_20), .col15(main_6_out_5),
    .col16(main_6_out_9), .col17(main_6_out_13), .col18(main_6_out_17));
  Timofeev_Maksunova_Peshkov_24214_number_picker_main main_6 (
    .in_1(_5_o), .out_2(main_6_out_2), .out_3(main_6_out_3), .out_4(main_6_out_4), .out_5(main_6_out_5),
    .out_6(main_6_out_6), .out_7(main_6_out_7), .out_8(main_6_out_8), .out_9(main_6_out_9),
    .out_10(main_6_out_10), .out_11(main_6_out_11), .out_12(main_6_out_12), .out_13(main_6_out_13),
    .out_14(main_6_out_14), .out_15(main_6_out_15), .out_16(main_6_out_16), .out_17(main_6_out_17),
    .out_18(main_6_out_18), .out_19(main_6_out_19), .out_20(main_6_out_20));
  DotMatrix #(.matrixcols(19), .matrixrows(19)) dotmatrix_7 (
    .col0(main_7_out_2), .col1(main_7_out_6), .col2(main_7_out_10), .col3(main_7_out_14),
    .col4(main_7_out_18), .col5(main_7_out_3), .col6(main_7_out_7), .col7(main_7_out_11),
    .col8(main_7_out_15), .col9(main_7_out_19), .col10(main_7_out_4), .col11(main_7_out_8),
    .col12(main_7_out_12), .col13(main_7_out_16), .col14(main_7_out_20), .col15(main_7_out_5),
    .col16(main_7_out_9), .col17(main_7_out_13), .col18(main_7_out_17));
  Timofeev_Maksunova_Peshkov_24214_number_picker_main main_7 (
    .in_1(_9_o), .out_2(main_7_out_2), .out_3(main_7_out_3), .out_4(main_7_out_4), .out_5(main_7_out_5),
    .out_6(main_7_out_6), .out_7(main_7_out_7), .out_8(main_7_out_8), .out_9(main_7_out_9),
    .out_10(main_7_out_10), .out_11(main_7_out_11), .out_12(main_7_out_12), .out_13(main_7_out_13),
    .out_14(main_7_out_14), .out_15(main_7_out_15), .out_16(main_7_out_16), .out_17(main_7_out_17),
    .out_18(main_7_out_18), .out_19(main_7_out_19), .out_20(main_7_out_20));
  DotMatrix #(.matrixcols(19), .matrixrows(19)) dotmatrix_8 (
    .col0(main_8_out_2), .col1(main_8_out_6), .col2(main_8_out_10), .col3(main_8_out_14),
    .col4(main_8_out_18), .col5(main_8_out_3), .col6(main_8_out_7), .col7(main_8_out_11),
    .col8(main_8_out_15), .col9(main_8_out_19), .col10(main_8_out_4), .col11(main_8_out_8),
    .col12(main_8_out_12), .col13(main_8_out_16), .col14(main_8_out_20), .col15(main_8_out_5),
    .col16(main_8_out_9), .col17(main_8_out_13), .col18(main_8_out_17));
  Timofeev_Maksunova_Peshkov_24214_number_picker_main main_8 (
    .in_1(_13_o), .out_2(main_8_out_2), .out_3(main_8_out_3), .out_4(main_8_out_4), .out_5(main_8_out_5),
    .out_6(main_8_out_6), .out_7(main_8_out_7), .out_8(main_8_out_8), .out_9(main_8_out_9),
    .out_10(main_8_out_10), .out_11(main_8_out_11), .out_12(main_8_out_12), .out_13(main_8_out_13),
    .out_14(main_8_out_14), .out_15(main_8_out_15), .out_16(main_8_out_16), .out_17(main_8_out_17),
    .out_18(main_8_out_18), .out_19(main_8_out_19), .out_20(main_8_out_20));
  Comparator #(.width(16), .mode("unsigned")) comparator_11 (
    .a(16'hfef8), .b(address_bus), .eq(comparator_11_eq));  // open: gt, lt
  Multiplexer #(.width(16), .enable("false")) multiplexer_4 (
    .in0(multiplexer_3_out), .in1({{15{1'b0}}, is_ai}), .out(data), .sel(comparator_11_eq));
  LED led_4 (.in(ready));
  Button button_1 (.out(U));
  Button button_2 (.out(L));
  Button button_3 (.out(D));
  Button button_4 (.out(R));
  Timofeev_Maksunova_Peshkov_24214_number_picker_main main_9 (
    .in_1(_2_o), .out_2(main_9_out_2), .out_3(main_9_out_3), .out_4(main_9_out_4), .out_5(main_9_out_5),
    .out_6(main_9_out_6), .out_7(main_9_out_7), .out_8(main_9_out_8), .out_9(main_9_out_9),
    .out_10(main_9_out_10), .out_11(main_9_out_11), .out_12(main_9_out_12), .out_13(main_9_out_13),
    .out_14(main_9_out_14), .out_15(main_9_out_15), .out_16(main_9_out_16), .out_17(main_9_out_17),
    .out_18(main_9_out_18), .out_19(main_9_out_19), .out_20(main_9_out_20));
  DotMatrix #(.matrixcols(19), .matrixrows(19)) dotmatrix_9 (
    .col0(main_9_out_2), .col1(main_9_out_6), .col2(main_9_out_10), .col3(main_9_out_14),
    .col4(main_9_out_18), .col5(main_9_out_3), .col6(main_9_out_7), .col7(main_9_out_11),
    .col8(main_9_out_15), .col9(main_9_out_19), .col10(main_9_out_4), .col11(main_9_out_8),
    .col12(main_9_out_12), .col13(main_9_out_16), .col14(main_9_out_20), .col15(main_9_out_5),
    .col16(main_9_out_9), .col17(main_9_out_13), .col18(main_9_out_17));
  DotMatrix #(.matrixcols(19), .matrixrows(19)) dotmatrix_10 (
    .col0(main_10_out_2), .col1(main_10_out_6), .col2(main_10_out_10), .col3(main_10_out_14),
    .col4(main_10_out_18), .col5(main_10_out_3), .col6(main_10_out_7), .col7(main_10_out_11),
    .col8(main_10_out_15), .col9(main_10_out_19), .col10(main_10_out_4), .col11(main_10_out_8),
    .col12(main_10_out_12), .col13(main_10_out_16), .col14(main_10_out_20), .col15(main_10_out_5),
    .col16(main_10_out_9), .col17(main_10_out_13), .col18(main_10_out_17));
  Timofeev_Maksunova_Peshkov_24214_number_picker_main main_10 (
    .in_1(_6_o), .out_2(main_10_out_2), .out_3(main_10_out_3), .out_4(main_10_out_4), .out_5(main_10_out_5),
    .out_6(main_10_out_6), .out_7(main_10_out_7), .out_8(main_10_out_8), .out_9(main_10_out_9),
    .out_10(main_10_out_10), .out_11(main_10_out_11), .out_12(main_10_out_12), .out_13(main_10_out_13),
    .out_14(main_10_out_14), .out_15(main_10_out_15), .out_16(main_10_out_16), .out_17(main_10_out_17),
    .out_18(main_10_out_18), .out_19(main_10_out_19), .out_20(main_10_out_20));
  DotMatrix #(.matrixcols(19), .matrixrows(19)) dotmatrix_11 (
    .col0(main_11_out_2), .col1(main_11_out_6), .col2(main_11_out_10), .col3(main_11_out_14),
    .col4(main_11_out_18), .col5(main_11_out_3), .col6(main_11_out_7), .col7(main_11_out_11),
    .col8(main_11_out_15), .col9(main_11_out_19), .col10(main_11_out_4), .col11(main_11_out_8),
    .col12(main_11_out_12), .col13(main_11_out_16), .col14(main_11_out_20), .col15(main_11_out_5),
    .col16(main_11_out_9), .col17(main_11_out_13), .col18(main_11_out_17));
  Timofeev_Maksunova_Peshkov_24214_number_picker_main main_11 (
    .in_1(_10_o), .out_2(main_11_out_2), .out_3(main_11_out_3), .out_4(main_11_out_4), .out_5(main_11_out_5),
    .out_6(main_11_out_6), .out_7(main_11_out_7), .out_8(main_11_out_8), .out_9(main_11_out_9),
    .out_10(main_11_out_10), .out_11(main_11_out_11), .out_12(main_11_out_12), .out_13(main_11_out_13),
    .out_14(main_11_out_14), .out_15(main_11_out_15), .out_16(main_11_out_16), .out_17(main_11_out_17),
    .out_18(main_11_out_18), .out_19(main_11_out_19), .out_20(main_11_out_20));
  Timofeev_Maksunova_Peshkov_24214_number_picker_main main_12 (
    .in_1(_14_o), .out_2(main_12_out_2), .out_3(main_12_out_3), .out_4(main_12_out_4), .out_5(main_12_out_5),
    .out_6(main_12_out_6), .out_7(main_12_out_7), .out_8(main_12_out_8), .out_9(main_12_out_9),
    .out_10(main_12_out_10), .out_11(main_12_out_11), .out_12(main_12_out_12), .out_13(main_12_out_13),
    .out_14(main_12_out_14), .out_15(main_12_out_15), .out_16(main_12_out_16), .out_17(main_12_out_17),
    .out_18(main_12_out_18), .out_19(main_12_out_19), .out_20(main_12_out_20));
  DotMatrix #(.matrixcols(19), .matrixrows(19)) dotmatrix_12 (
    .col0(main_12_out_2), .col1(main_12_out_6), .col2(main_12_out_10), .col3(main_12_out_14),
    .col4(main_12_out_18), .col5(main_12_out_3), .col6(main_12_out_7), .col7(main_12_out_11),
    .col8(main_12_out_15), .col9(main_12_out_19), .col10(main_12_out_4), .col11(main_12_out_8),
    .col12(main_12_out_12), .col13(main_12_out_16), .col14(main_12_out_20), .col15(main_12_out_5),
    .col16(main_12_out_9), .col17(main_12_out_13), .col18(main_12_out_17));
  LED led_5 (.in(is_ai));
  Button button_5 (.out(button_5_out));
  DotMatrix #(.matrixcols(19), .matrixrows(19)) dotmatrix_13 (
    .col0(main_13_out_2), .col1(main_13_out_6), .col2(main_13_out_10), .col3(main_13_out_14),
    .col4(main_13_out_18), .col5(main_13_out_3), .col6(main_13_out_7), .col7(main_13_out_11),
    .col8(main_13_out_15), .col9(main_13_out_19), .col10(main_13_out_4), .col11(main_13_out_8),
    .col12(main_13_out_12), .col13(main_13_out_16), .col14(main_13_out_20), .col15(main_13_out_5),
    .col16(main_13_out_9), .col17(main_13_out_13), .col18(main_13_out_17));
  Timofeev_Maksunova_Peshkov_24214_number_picker_main main_13 (
    .in_1(_3_o), .out_2(main_13_out_2), .out_3(main_13_out_3), .out_4(main_13_out_4), .out_5(main_13_out_5),
    .out_6(main_13_out_6), .out_7(main_13_out_7), .out_8(main_13_out_8), .out_9(main_13_out_9),
    .out_10(main_13_out_10), .out_11(main_13_out_11), .out_12(main_13_out_12), .out_13(main_13_out_13),
    .out_14(main_13_out_14), .out_15(main_13_out_15), .out_16(main_13_out_16), .out_17(main_13_out_17),
    .out_18(main_13_out_18), .out_19(main_13_out_19), .out_20(main_13_out_20));
  Timofeev_Maksunova_Peshkov_24214_number_picker_main main_14 (
    .in_1(_7_o), .out_2(main_14_out_2), .out_3(main_14_out_3), .out_4(main_14_out_4), .out_5(main_14_out_5),
    .out_6(main_14_out_6), .out_7(main_14_out_7), .out_8(main_14_out_8), .out_9(main_14_out_9),
    .out_10(main_14_out_10), .out_11(main_14_out_11), .out_12(main_14_out_12), .out_13(main_14_out_13),
    .out_14(main_14_out_14), .out_15(main_14_out_15), .out_16(main_14_out_16), .out_17(main_14_out_17),
    .out_18(main_14_out_18), .out_19(main_14_out_19), .out_20(main_14_out_20));
  DotMatrix #(.matrixcols(19), .matrixrows(19)) dotmatrix_14 (
    .col0(main_14_out_2), .col1(main_14_out_6), .col2(main_14_out_10), .col3(main_14_out_14),
    .col4(main_14_out_18), .col5(main_14_out_3), .col6(main_14_out_7), .col7(main_14_out_11),
    .col8(main_14_out_15), .col9(main_14_out_19), .col10(main_14_out_4), .col11(main_14_out_8),
    .col12(main_14_out_12), .col13(main_14_out_16), .col14(main_14_out_20), .col15(main_14_out_5),
    .col16(main_14_out_9), .col17(main_14_out_13), .col18(main_14_out_17));
  DotMatrix #(.matrixcols(19), .matrixrows(19)) dotmatrix_15 (
    .col0(main_15_out_2), .col1(main_15_out_6), .col2(main_15_out_10), .col3(main_15_out_14),
    .col4(main_15_out_18), .col5(main_15_out_3), .col6(main_15_out_7), .col7(main_15_out_11),
    .col8(main_15_out_15), .col9(main_15_out_19), .col10(main_15_out_4), .col11(main_15_out_8),
    .col12(main_15_out_12), .col13(main_15_out_16), .col14(main_15_out_20), .col15(main_15_out_5),
    .col16(main_15_out_9), .col17(main_15_out_13), .col18(main_15_out_17));
  Timofeev_Maksunova_Peshkov_24214_number_picker_main main_15 (
    .in_1(_11_o), .out_2(main_15_out_2), .out_3(main_15_out_3), .out_4(main_15_out_4), .out_5(main_15_out_5),
    .out_6(main_15_out_6), .out_7(main_15_out_7), .out_8(main_15_out_8), .out_9(main_15_out_9),
    .out_10(main_15_out_10), .out_11(main_15_out_11), .out_12(main_15_out_12), .out_13(main_15_out_13),
    .out_14(main_15_out_14), .out_15(main_15_out_15), .out_16(main_15_out_16), .out_17(main_15_out_17),
    .out_18(main_15_out_18), .out_19(main_15_out_19), .out_20(main_15_out_20));
  DotMatrix #(.matrixcols(19), .matrixrows(19)) dotmatrix_16 (
    .col0(main_16_out_2), .col1(main_16_out_6), .col2(main_16_out_10), .col3(main_16_out_14),
    .col4(main_16_out_18), .col5(main_16_out_3), .col6(main_16_out_7), .col7(main_16_out_11),
    .col8(main_16_out_15), .col9(main_16_out_19), .col10(main_16_out_4), .col11(main_16_out_8),
    .col12(main_16_out_12), .col13(main_16_out_16), .col14(main_16_out_20), .col15(main_16_out_5),
    .col16(main_16_out_9), .col17(main_16_out_13), .col18(main_16_out_17));
  Timofeev_Maksunova_Peshkov_24214_number_picker_main main_16 (
    .in_1(_15_o), .out_2(main_16_out_2), .out_3(main_16_out_3), .out_4(main_16_out_4), .out_5(main_16_out_5),
    .out_6(main_16_out_6), .out_7(main_16_out_7), .out_8(main_16_out_8), .out_9(main_16_out_9),
    .out_10(main_16_out_10), .out_11(main_16_out_11), .out_12(main_16_out_12), .out_13(main_16_out_13),
    .out_14(main_16_out_14), .out_15(main_16_out_15), .out_16(main_16_out_16), .out_17(main_16_out_17),
    .out_18(main_16_out_18), .out_19(main_16_out_19), .out_20(main_16_out_20));
  Register #(.width(1)) register_21 (.D(button_5_out), .Q(is_ai), .clk(button_5_out), .clr(button_6_out));  // open: en
  LED #(.active("false")) led_6 (.in(is_ai));
  Button button_6 (.out(button_6_out));

  // Other names for the same wires on the sheet: RAM[15:0] = data_bus

  // Notes on the sheet:
  //   instructions memory
  //   there should be img-file
  //   Simulating
  //   Evaluating
  //   Choosing move
  //   Ready
  //   AI
  //   HUMAN
endmodule

module random (
  input  in_1,
  output [15:0] out_2
);

  Random #(.width(4)) random_1 (.clk(in_1), .out(out_2[3:0]));  // open: next, clr

  assign out_2[15:4] = {12{1'b0}};
endmodule

module small_comparator (
  input  [3:0] in_1,
  input  [3:0] in_2,
  output out_3
);

  Comparator #(.width(4)) comparator_1 (.a(in_1), .b(in_2), .eq(out_3));  // open: gt, lt
endmodule

module game_over_check (
  input  [3:0] _0,
  input  [3:0] _1,
  input  [3:0] _2,
  input  [3:0] _3,
  input  [3:0] _4,
  input  [3:0] _5,
  input  [3:0] _6,
  input  [3:0] _7,
  input  [3:0] _8,
  input  [3:0] _9,
  input  [3:0] _10,
  input  [3:0] _11,
  input  [3:0] _12,
  input  [3:0] _13,
  input  [3:0] _14,
  input  [3:0] _15,
  output [15:0] \end 
);

  wire and_1_out, not_1_out, not_2_out, not_3_out, or_1_out, or_2_out, or_3_out, or_5_out,
       small_comparator_1_out_3, small_comparator_2_out_3, small_comparator_3_out_3,
       small_comparator_4_out_3, small_comparator_5_out_3, small_comparator_6_out_3,
       small_comparator_7_out_3, small_comparator_8_out_3, small_comparator_9_out_3,
       small_comparator_10_out_3, small_comparator_11_out_3, small_comparator_12_out_3,
       small_comparator_13_out_3, small_comparator_14_out_3, small_comparator_15_out_3,
       small_comparator_16_out_3, small_comparator_17_out_3, small_comparator_18_out_3,
       small_comparator_19_out_3, small_comparator_20_out_3, small_comparator_21_out_3,
       small_comparator_22_out_3, small_comparator_23_out_3, small_comparator_24_out_3,
       small_comparator_25_out_3, small_comparator_26_out_3, small_comparator_27_out_3,
       small_comparator_28_out_3, small_comparator_29_out_3, small_comparator_30_out_3,
       small_comparator_31_out_3, small_comparator_32_out_3, small_comparator_33_out_3,
       small_comparator_34_out_3, small_comparator_35_out_3, small_comparator_36_out_3,
       small_comparator_37_out_3, small_comparator_38_out_3, small_comparator_39_out_3,
       small_comparator_40_out_3, small_comparator_41_out_3, small_comparator_42_out_3,
       small_comparator_43_out_3, small_comparator_44_out_3, small_comparator_45_out_3,
       small_comparator_46_out_3, small_comparator_47_out_3, small_comparator_48_out_3,
       small_comparator_49_out_3, small_comparator_50_out_3, small_comparator_51_out_3,
       small_comparator_52_out_3, small_comparator_53_out_3, small_comparator_54_out_3,
       small_comparator_55_out_3, small_comparator_56_out_3;

  small_comparator small_comparator_1 (.in_1(_0), .in_2(_4), .out_3(small_comparator_1_out_3));
  small_comparator small_comparator_2 (.in_1(_1), .in_2(_5), .out_3(small_comparator_2_out_3));
  small_comparator small_comparator_3 (.in_1(_2), .in_2(_6), .out_3(small_comparator_3_out_3));
  small_comparator small_comparator_4 (.in_1(_3), .in_2(_7), .out_3(small_comparator_4_out_3));
  small_comparator small_comparator_5 (.in_1(_4), .in_2(_8), .out_3(small_comparator_5_out_3));
  small_comparator small_comparator_6 (.in_1(_5), .in_2(_9), .out_3(small_comparator_6_out_3));
  small_comparator small_comparator_7 (.in_1(_6), .in_2(_10), .out_3(small_comparator_7_out_3));
  small_comparator small_comparator_8 (.in_1(_7), .in_2(_11), .out_3(small_comparator_8_out_3));
  small_comparator small_comparator_9 (.in_1(_8), .in_2(_12), .out_3(small_comparator_9_out_3));
  small_comparator small_comparator_10 (.in_1(_9), .in_2(_13), .out_3(small_comparator_10_out_3));
  small_comparator small_comparator_11 (.in_1(_10), .in_2(_14), .out_3(small_comparator_11_out_3));
  small_comparator small_comparator_12 (.in_1(_11), .in_2(_15), .out_3(small_comparator_12_out_3));
  or or_1 (or_1_out, small_comparator_1_out_3, small_comparator_2_out_3, small_comparator_3_out_3, small_comparator_4_out_3, small_comparator_5_out_3, small_comparator_6_out_3, small_comparator_7_out_3, small_comparator_8_out_3, small_comparator_9_out_3, small_comparator_10_out_3, small_comparator_11_out_3, small_comparator_12_out_3);
  small_comparator small_comparator_13 (.in_1(4'b1011), .in_2(_0), .out_3(small_comparator_13_out_3));
  small_comparator small_comparator_14 (.in_1(4'b1011), .in_2(_1), .out_3(small_comparator_14_out_3));
  small_comparator small_comparator_15 (.in_1(4'b1011), .in_2(_2), .out_3(small_comparator_15_out_3));
  small_comparator small_comparator_16 (.in_1(4'b1011), .in_2(_3), .out_3(small_comparator_16_out_3));
  small_comparator small_comparator_17 (.in_1(4'b1011), .in_2(_4), .out_3(small_comparator_17_out_3));
  small_comparator small_comparator_18 (.in_1(4'b1011), .in_2(_5), .out_3(small_comparator_18_out_3));
  small_comparator small_comparator_19 (.in_1(4'b1011), .in_2(_6), .out_3(small_comparator_19_out_3));
  small_comparator small_comparator_20 (.in_1(4'b1011), .in_2(_7), .out_3(small_comparator_20_out_3));
  small_comparator small_comparator_21 (.in_1(4'b1011), .in_2(_8), .out_3(small_comparator_21_out_3));
  small_comparator small_comparator_22 (.in_1(4'b1011), .in_2(_9), .out_3(small_comparator_22_out_3));
  small_comparator small_comparator_23 (.in_1(4'b1011), .in_2(_10), .out_3(small_comparator_23_out_3));
  small_comparator small_comparator_24 (.in_1(4'b1011), .in_2(_11), .out_3(small_comparator_24_out_3));
  small_comparator small_comparator_25 (.in_1(4'b1011), .in_2(_12), .out_3(small_comparator_25_out_3));
  small_comparator small_comparator_26 (.in_1(4'b1011), .in_2(_13), .out_3(small_comparator_26_out_3));
  small_comparator small_comparator_27 (.in_1(4'b1011), .in_2(_14), .out_3(small_comparator_27_out_3));
  small_comparator small_comparator_28 (.in_1(4'b1011), .in_2(_15), .out_3(small_comparator_28_out_3));
  not not_1 (not_1_out, or_1_out);
  small_comparator small_comparator_29 (.in_1(_0), .in_2(_1), .out_3(small_comparator_29_out_3));
  small_comparator small_comparator_30 (.in_1(_1), .in_2(_2), .out_3(small_comparator_30_out_3));
  small_comparator small_comparator_31 (.in_1(_2), .in_2(_3), .out_3(small_comparator_31_out_3));
  small_comparator small_comparator_32 (.in_1(_4), .in_2(_5), .out_3(small_comparator_32_out_3));
  small_comparator small_comparator_33 (.in_1(_5), .in_2(_6), .out_3(small_comparator_33_out_3));
  small_comparator small_comparator_34 (.in_1(_6), .in_2(_7), .out_3(small_comparator_34_out_3));
  small_comparator small_comparator_35 (.in_1(_8), .in_2(_9), .out_3(small_comparator_35_out_3));
  small_comparator small_comparator_36 (.in_1(_9), .in_2(_10), .out_3(small_comparator_36_out_3));
  small_comparator small_comparator_37 (.in_1(_10), .in_2(_11), .out_3(small_comparator_37_out_3));
  small_comparator small_comparator_38 (.in_1(_12), .in_2(_13), .out_3(small_comparator_38_out_3));
  small_comparator small_comparator_39 (.in_1(_13), .in_2(_14), .out_3(small_comparator_39_out_3));
  small_comparator small_comparator_40 (.in_1(_14), .in_2(_15), .out_3(small_comparator_40_out_3));
  or or_2 (or_2_out, small_comparator_13_out_3, small_comparator_14_out_3, small_comparator_15_out_3, small_comparator_16_out_3, small_comparator_17_out_3, small_comparator_18_out_3, small_comparator_19_out_3, small_comparator_20_out_3, small_comparator_21_out_3, small_comparator_22_out_3, small_comparator_23_out_3, small_comparator_24_out_3, small_comparator_25_out_3, small_comparator_26_out_3, small_comparator_27_out_3, small_comparator_28_out_3);
  or or_3 (or_3_out, small_comparator_29_out_3, small_comparator_30_out_3, small_comparator_31_out_3, small_comparator_32_out_3, small_comparator_33_out_3, small_comparator_34_out_3, small_comparator_35_out_3, small_comparator_36_out_3, small_comparator_37_out_3, small_comparator_38_out_3, small_comparator_39_out_3, small_comparator_40_out_3);
  and and_1 (and_1_out, not_1_out, not_2_out, not_3_out);
  not not_2 (not_2_out, or_3_out);
  or or_4 (\end [0], or_2_out, and_1_out);
  small_comparator small_comparator_41 (.in_1(4'b0000), .in_2(_0), .out_3(small_comparator_41_out_3));
  small_comparator small_comparator_42 (.in_1(4'b0000), .in_2(_1), .out_3(small_comparator_42_out_3));
  small_comparator small_comparator_43 (.in_1(4'b0000), .in_2(_2), .out_3(small_comparator_43_out_3));
  small_comparator small_comparator_44 (.in_1(4'b0000), .in_2(_3), .out_3(small_comparator_44_out_3));
  small_comparator small_comparator_45 (.in_1(4'b0000), .in_2(_4), .out_3(small_comparator_45_out_3));
  small_comparator small_comparator_46 (.in_1(4'b0000), .in_2(_5), .out_3(small_comparator_46_out_3));
  small_comparator small_comparator_47 (.in_1(4'b0000), .in_2(_6), .out_3(small_comparator_47_out_3));
  small_comparator small_comparator_48 (.in_1(4'b0000), .in_2(_7), .out_3(small_comparator_48_out_3));
  small_comparator small_comparator_49 (.in_1(4'b0000), .in_2(_8), .out_3(small_comparator_49_out_3));
  small_comparator small_comparator_50 (.in_1(4'b0000), .in_2(_9), .out_3(small_comparator_50_out_3));
  small_comparator small_comparator_51 (.in_1(4'b0000), .in_2(_10), .out_3(small_comparator_51_out_3));
  small_comparator small_comparator_52 (.in_1(4'b0000), .in_2(_11), .out_3(small_comparator_52_out_3));
  small_comparator small_comparator_53 (.in_1(4'b0000), .in_2(_12), .out_3(small_comparator_53_out_3));
  small_comparator small_comparator_54 (.in_1(4'b0000), .in_2(_13), .out_3(small_comparator_54_out_3));
  small_comparator small_comparator_55 (.in_1(4'b0000), .in_2(_14), .out_3(small_comparator_55_out_3));
  small_comparator small_comparator_56 (.in_1(4'b0000), .in_2(_15), .out_3(small_comparator_56_out_3));
  not not_3 (not_3_out, or_5_out);
  or or_5 (or_5_out, small_comparator_41_out_3, small_comparator_42_out_3, small_comparator_43_out_3, small_comparator_44_out_3, small_comparator_45_out_3, small_comparator_46_out_3, small_comparator_47_out_3, small_comparator_48_out_3, small_comparator_49_out_3, small_comparator_50_out_3, small_comparator_51_out_3, small_comparator_52_out_3, small_comparator_53_out_3, small_comparator_54_out_3, small_comparator_55_out_3, small_comparator_56_out_3);

  assign \end [15:1] = {15{1'b0}};

  // Other names for the same wires on the sheet: _0_pow[3:0] = _0; _1_pow[3:0] = _1; _2_pow[3:0] = _2;
  //   _3_pow[3:0] = _3; _4_pow[3:0] = _4; _5_pow[3:0] = _5; _6_pow[3:0] = _6; _7_pow[3:0] = _7; _8_pow[3:0] = _8;
  //   _9_pow[3:0] = _9; _10_pow[3:0] = _10; _11_pow[3:0] = _11; _12_pow[3:0] = _12; _13_pow[3:0] = _13;
  //   _14_pow[3:0] = _14; _15_pow[3:0] = _15

  // Notes on the sheet:
  //   Vertical neighbours
  //   game or end
  //   0 or 1
  //   Horizontal neighbours
endmodule

module input_controller (
  input  LEFT,
  input  in_2,
  input  DOWN,
  input  in_4,
  output [15:0] out_5
);


  assign out_5 = {{12{1'b0}}, in_4, DOWN, in_2, LEFT};

  // Notes on the sheet:
  //   RIGHT
  //   UP
endmodule
