// Logisim project Timofeev_Maksunova_Peshkov_24214_numbers.circ as structural Verilog
module _1 (
);

  DotMatrix #(.matrixcols(19), .matrixrows(19)) dotmatrix_1 (
    .col0({19{1'b0}}), .col1(19'h400), .col2(19'h800), .col3(19'h1fc0));  // open: col4, col5, col6, col7, col8, col9, col10, col11, col12, col13, col14, col15, col16, col17, col18
endmodule

module _2 (
);

  DotMatrix #(.matrixcols(19), .matrixrows(19)) dotmatrix_1 (
    .col0(19'h8c0), .col1(19'h1140), .col2(19'h1140), .col3(19'he40));  // open: col4, col5, col6, col7, col8, col9, col10, col11, col12, col13, col14, col15, col16, col17, col18
endmodule

module _3 (
);

  DotMatrix #(.matrixcols(19), .matrixrows(19)) dotmatrix_1 (
    .col0(19'h880), .col1(19'h1240), .col2(19'h1240), .col3(19'hd80));  // open: col4, col5, col6, col7, col8, col9, col10, col11, col12, col13, col14, col15, col16, col17, col18
endmodule

module _4 (
);

  DotMatrix #(.matrixcols(19), .matrixrows(19)) dotmatrix_1 (
    .col0(19'h1e00), .col1(19'h200), .col2(19'h200), .col3(19'h1fc0));  // open: col4, col5, col6, col7, col8, col9, col10, col11, col12, col13, col14, col15, col16, col17, col18
endmodule

module _5 (
);

  DotMatrix #(.matrixcols(19), .matrixrows(19)) dotmatrix_1 (
    .col0(19'h1e40), .col1(19'h1240), .col2(19'h1240), .col3(19'h1180));  // open: col4, col5, col6, col7, col8, col9, col10, col11, col12, col13, col14, col15, col16, col17, col18
endmodule

module _6 (
);

  DotMatrix #(.matrixcols(19), .matrixrows(19)) dotmatrix_1 (
    .col0(19'h780), .col1(19'ha40), .col2(19'h1240), .col3(19'h180));  // open: col4, col5, col6, col7, col8, col9, col10, col11, col12, col13, col14, col15, col16, col17, col18
endmodule

module _7 (
);

  DotMatrix #(.matrixcols(19), .matrixrows(19)) dotmatrix_1 (
    .col0(19'h1000), .col1(19'h11c0), .col2(19'h1200), .col3(19'h1c00));  // open: col4, col5, col6, col7, col8, col9, col10, col11, col12, col13, col14, col15, col16, col17, col18
endmodule

module _8 (
);

  DotMatrix #(.matrixcols(19), .matrixrows(19)) dotmatrix_1 (
    .col0(19'hd80), .col1(19'h1240), .col2(19'h1240), .col3(19'hd80));  // open: col4, col5, col6, col7, col8, col9, col10, col11, col12, col13, col14, col15, col16, col17, col18
endmodule

module _9 (
);

  DotMatrix #(.matrixcols(19), .matrixrows(19)) dotmatrix_1 (
    .col0(19'hc00), .col1(19'h1240), .col2(19'h1280), .col3(19'hf00));  // open: col4, col5, col6, col7, col8, col9, col10, col11, col12, col13, col14, col15, col16, col17, col18
endmodule

module _0 (
);

  DotMatrix #(.matrixcols(19), .matrixrows(19)) dotmatrix_1 (
    .col0(19'hf80), .col1(19'h1040), .col2(19'h1040), .col3(19'hf80));  // open: col4, col5, col6, col7, col8, col9, col10, col11, col12, col13, col14, col15, col16, col17, col18
endmodule
